# Fritzing sketch fritzing (saved by Fritzing 0.9.3b)
breadboards: 1

parts:
  IC1 = L293D [package=THT]
  U1 = NodeMCU V1.0
  M1 = DC Motor
  M2 = DC Motor
  U2 = 74HC04_HEX_INVERTER [package=dil14]
  JP1 = Header 6 [package=1x06-smd]
  JP2 = Header 6 [package=1x06-smd]
  JP3 = Header 6 [package=1x06-smd]

nets:
  N1: IC1.Enable_1, JP1.6
  N2: IC1.In_1, JP1.5
  N3: IC1.Out_1_(_Controlled_by_Enable_1_), M2.pin_1
  GND: IC1.0V, U1.GND
  N4: IC1.Out_2_(_Controlled_by_Enable_1_), M2.pin_2
  N5: IC1.In_2, JP1.4
  5V: IC1.+Vmotor, IC1.+V
  N6: IC1.Enable_2, JP1.3
  N7: IC1.In_3, JP1.2
  N8: IC1.Out_3_(_Controlled_by_Enable_2_), M1.pin_2
  N9: IC1.Out_4_(_Controlled_by_Enable_2_), M1.pin_1
  N10: IC1.In_4, JP1.1
  N11: U1.D0, U2.1A, JP2.2
  N12: U1.D1, JP2.1
  N13: U1.D2, U2.2A, JP2.5
  N14: U1.D3, JP2.4
  N15: U1.D4, JP3.1
  N16: U1.D5, U2.5A
  N17: U1.D6, JP3.2
  N18: U1.D7, JP3.4
  N19: U1.D8, JP3.5
  N20: U2.1Y, JP2.3
  N21: U2.2Y, JP2.6
  N22: U2.5Y, JP3.3
  N23: U2.6Y, JP3.6

custom parts:
  NodeMCU V1.0: ESP8266 based NodeMCU
